// Digital circuit cpu.dig as structural Verilog
module cpu (
  input  in_1,
  input  clk,
  input  in_3,
  input  [4:0] in_4,
  output [31:0] out_5,
  output [31:0] out_6,
  output [31:0] out_7,
  output [31:0] out_8,
  output [31:0] out_9,
  output [31:0] out_10,
  output [31:0] out_11,
  output out_12,
  output out_13
);

  wire u_riscv_cpu_dmem_we_o;
  wire [31:0] ramdualport_1_d, rom_1_d, u_riscv_cpu_dmem_addr_o, u_riscv_cpu_dmem_wdata_o,
       u_riscv_cpu_imem_addr_o;

  riscv_cpu #(.applicationType("GHDL"), .ghdlOptions("--std=08 --ieee=synopsys --workdir=\"C:\\Users\\RiverNet\\Documents\\Coding\\RiscVtrabalho\\RISC-V-EEL580---Computer-Architecture-meu\""), .CodeFile("C:\\Users\\RiverNet\\Documents\\Coding\\RiscVtrabalho\\RISC-V-EEL580---Computer-Architecture-meu\\riscv_cpu.vhd")) u_riscv_cpu (
    .clk_i(clk), .reset_i(in_3), .load_enable_i(in_3), .imem_data_i(rom_1_d), .dmem_rdata_i(ramdualport_1_d),
    .reg_sel_i(in_4), .imem_addr_o(u_riscv_cpu_imem_addr_o), .dmem_addr_o(u_riscv_cpu_dmem_addr_o),
    .dmem_wdata_o(u_riscv_cpu_dmem_wdata_o), .dmem_we_o(u_riscv_cpu_dmem_we_o), .pc_debug_o(out_10),
    .instr_debug_o(out_9), .alu_result_debug_o(out_5), .reg_debug_o(out_6), .stage_if_pc_o(out_7),
    .stage_id_pc_o(out_8), .stage_ex_pc_o(out_11), .hazard_stall_o(out_12), .hazard_flush_o(out_13));
  ROM #(.AddrBits(8), .Bits(32)) rom_1 (.A(u_riscv_cpu_imem_addr_o[9:2]), .sel(in_1), .D(rom_1_d));
  RAMDualPort #(.AddrBits(8), .Bits(32)) ramdualport_1 (
    .A(u_riscv_cpu_dmem_addr_o[9:2]), .Din(u_riscv_cpu_dmem_wdata_o), .str(u_riscv_cpu_dmem_we_o), .C(clk),
    .ld(in_1), .D(ramdualport_1_d));

  // Notes on the sheet:
  //   contents of rom_1 (hex, n*v repeats v):
  //   ef,4006f,ffc006f,8067
  //   Program Counter
  //   Instrução
  //   Resultado da ALU
  //   Registrador (selecione no botão inferior na esquerda)
  //   Estágio de IF
  //   Estágio de ID
  //   Estágio de EX
  //   Stall
  //   Flush
endmodule
