// Digital circuit cpu.dig as structural Verilog
module cpu (
  input  clk,
  input  in_2,
  input  [4:0] in_3,
  input  in_13,
  output [31:0] out_4,
  output [31:0] out_5,
  output out_6,
  output out_7,
  output [31:0] out_8,
  output [31:0] out_9,
  output out_10,
  output out_11,
  output out_12,
  output [31:0] out_14
);

  wire \u_Cpu_não_vetorial_write_to_ram ;
  wire [31:0] ramdualport_1_d, \u_Cpu_não_vetorial_out_to_ram , \u_Cpu_não_vetorial_ram_addr ,
       \u_Cpu_não_vetorial_rom_addr ;

  \Cpu_não_vetorial  #(.applicationType("GHDL"), .ghdlOptions("--std=08 --ieee=synopsys --workdir=\"C:\\Users\\RiverNet\\Documents\\Coding\\RiscVtrabalho\\RISC-V-EEL580---Computer-Architecture-meu\""), .CodeFile("C:\\Users\\RiverNet\\Documents\\Coding\\RiscVtrabalho\\RISC-V-EEL580---Computer-Architecture-meu\\riscv_cpu.vhd")) \u_Cpu_não_vetorial  (
    .Clock(clk), .Reset(in_2), .Instruction_data(out_8), .Ram_Data(ramdualport_1_d), .Sel_Registrador(in_3),
    .Rom_Addr(\u_Cpu_não_vetorial_rom_addr ), .Ram_addr(\u_Cpu_não_vetorial_ram_addr ),
    .Out_to_Ram(\u_Cpu_não_vetorial_out_to_ram ), .Write_to_Ram(\u_Cpu_não_vetorial_write_to_ram ),
    .PC_Counter(out_9), .Prev_Instruction(out_14), .ALU_Result(out_4), .Registrador_Debug(out_5),
    .ALU_Carry(out_6), .ALU_Overflow(out_7), .ALU_Zero(out_10), .Stall(out_11), .Flush(out_12));
  ROM #(.AddrBits(8), .Bits(32)) rom_1 (.A(\u_Cpu_não_vetorial_rom_addr [9:2]), .sel(in_13), .D(out_8));
  RAMDualPort #(.AddrBits(8), .Bits(32)) ramdualport_1 (
    .A(\u_Cpu_não_vetorial_ram_addr [9:2]), .Din(\u_Cpu_não_vetorial_out_to_ram ),
    .str(\u_Cpu_não_vetorial_write_to_ram ), .C(clk), .ld(in_13), .D(ramdualport_1_d));

  // Notes on the sheet:
  //   Selecionar Registrador
  //   Ligar Memorias
  //   Clock
  //   Reset
  //   contents of rom_1 (hex, n*v repeats v):
  //   fff00293,100313,6283b3,4*0,628063
  //   Program Counter Atual
  //   Instrução Atual (de um reset antes de iniciar)
  //   Instrução Anterior
  //   Resultado da ALU
  //   Registrador (selecione no botão inferior na esquerda)
  //   Carry na ALU
  //   Overflow na ALU
  //   Zero na ALU
  //   Stall
  //   Flush
endmodule
